// Logisim project basic_computer.circ as structural Verilog: 2 circuits, main circuit main
module main (
  input  MEM_LD,
  input  MEM_CLR,
  input  INC_AR,
  input  LD_AR,
  input  CLR_AR,
  input  MEM_WR,
  input  MEM_ON,
  input  LD_PC,
  input  INC_PC,
  input  CLR_PC,
  input  LD_DR,
  input  INC_DR,
  input  LD_AC,
  input  CLR_DR,
  input  INC_AC,
  input  LD_IR,
  input  [2:0] C2_C1_C0,
  input  CLR_AC,
  input  [2:0] S2S1S0,
  input  CLR_IR,
  input  INC_IR,
  input  LD_TR,
  input  INC_TR,
  input  CLR_TR
);

  wire CLK_out;
  wire [15:0] AC_q, alu_1_out, AR_q, DR_q, IR_q, multiplexer_1_out, PC_q, ram_1_data, TR_q;

  Clock CLK (.out(CLK_out));
  Counter #(.width(16), .max('hffff)) DR (
    .load(LD_DR), .D(multiplexer_1_out), .count(INC_DR), .Q(DR_q), .clk(CLK_out), .clr(CLR_DR));  // open: carry
  ALU alu_1 (.A(DR_q), .B(AC_q), .C2_C1_C0(C2_C1_C0), .OUT(alu_1_out));
  Counter #(.width(16), .max('hffff)) TR (
    .load(LD_TR), .D(multiplexer_1_out), .count(INC_TR), .Q(TR_q), .clk(CLK_out), .clr(CLR_TR));  // open: carry
  RAM #(.dataWidth(16), .bus("separate")) ram_1 (
    .addr(AR_q[7:0]), .din(multiplexer_1_out), .data(ram_1_data), .str(MEM_WR), .sel(MEM_ON), .clk(CLK_out),
    .ld(MEM_LD), .clr(MEM_CLR));
  Counter #(.width(16), .max('hffff)) AC (
    .load(LD_AC), .D(alu_1_out), .count(INC_AC), .Q(AC_q), .clk(CLK_out), .clr(CLR_AC));  // open: carry
  Counter #(.width(16), .max('hffff)) AR (
    .load(LD_AR), .D(multiplexer_1_out), .count(INC_AR), .Q(AR_q), .clk(CLK_out), .clr(CLR_AR));  // open: carry
  Counter #(.width(16), .max('hffff)) PC (
    .load(LD_PC), .D(multiplexer_1_out), .count(INC_PC), .Q(PC_q), .clk(CLK_out), .clr(CLR_PC));  // open: carry
  Counter #(.width(16), .max('hffff)) IR (
    .load(LD_IR), .D(multiplexer_1_out), .count(INC_IR), .Q(IR_q), .clk(CLK_out), .clr(CLR_IR));  // open: carry
  Multiplexer #(.select(3), .width(16)) multiplexer_1 (
    .in1(ram_1_data), .in2(AR_q), .in3(PC_q), .in4(DR_q), .in5(AC_q), .in6(IR_q), .in7(TR_q),
    .out(multiplexer_1_out), .sel(S2S1S0), .en(1'b1));  // open: in0
endmodule

module ALU (
  input  [15:0] A,
  input  [15:0] B,
  input  [2:0] C2_C1_C0,
  output [15:0] OUT
);

  wire [15:0] adder_1_out, divider_1_out, multiplier_1_out, not_1_out, subtractor_1_out, xor_1_out;

  Adder #(.width(16)) adder_1 (.a(A), .b(B), .out(adder_1_out), .cin(1'b0));  // open: cout
  Subtractor #(.width(16)) subtractor_1 (.a(A), .b(B), .out(subtractor_1_out), .bin(1'b0));  // open: bout
  Multiplier #(.width(16)) multiplier_1 (.a(A), .b(B), .out(multiplier_1_out), .cin({16{1'b0}}));  // open: cout
  Divider #(.width(16)) divider_1 (.a(A), .b(B), .out(divider_1_out), .upper({16{1'b0}}));  // open: rem
  assign not_1_out = ~A;  // NOT_Gate not_1, 16 bits wide
  assign xor_1_out = B ^ A;  // XOR_Gate xor_1, 16 bits wide
  Multiplexer #(.select(3), .width(16)) multiplexer_1 (
    .in1(A), .in2(adder_1_out), .in3(subtractor_1_out), .in4(multiplier_1_out), .in5(divider_1_out),
    .in6(not_1_out), .in7(xor_1_out), .out(OUT), .sel(C2_C1_C0), .en(1'b1));  // open: in0
endmodule
